// Logisim project 4bitCPU.circ as structural Verilog: 17 circuits, main circuit main
module main (
  input  [3:0] in_1,
  input  in_2,
  input  in_3,
  input  in_4,
  input  in_5,
  input  in_6,
  output out_7,
  output [3:0] out_8
);

  wire [2:0] cpu_reg_4_1_out_4;

  CPU_REG_4 cpu_reg_4_1 (.in_1(in_1), .in_2(in_2), .in_3(in_4), .out_4({out_7, cpu_reg_4_1_out_4}));
  CPU_REG_4 cpu_reg_4_2 (.in_1({cpu_reg_4_1_out_4, in_6}), .in_2(in_3), .in_3(in_5), .out_4(out_8));
endmodule

module CPU_MEM_1 (
  input  s,
  input  e,
  output q
);

  wire nand_1_out, nand_2_out, nand_4_out;

  nand nand_1 (nand_1_out, s, e);
  nand nand_2 (nand_2_out, e, nand_1_out);
  nand nand_3 (q, nand_1_out, nand_4_out);
  nand nand_4 (nand_4_out, q, nand_2_out);

  // Notes on the sheet:
  //   1 bit memory cell
endmodule

module CPU_MEM_4 (
  input  [3:0] in_1,
  input  in_2,
  output [3:0] out_3
);

  CPU_MEM_1 cpu_mem_1_1 (.s(in_1[0]), .e(in_2), .q(out_3[0]));
  CPU_MEM_1 cpu_mem_1_2 (.s(in_1[1]), .e(in_2), .q(out_3[1]));
  CPU_MEM_1 cpu_mem_1_3 (.s(in_1[2]), .e(in_2), .q(out_3[2]));
  CPU_MEM_1 cpu_mem_1_4 (.s(in_1[3]), .e(in_2), .q(out_3[3]));
endmodule

module CPU_REG_4 (
  input  [3:0] in_1,
  input  in_2,
  input  in_3,
  output [3:0] out_4
);

  wire [3:0] cpu_mem_4_1_out_3;

  CPU_MEM_4 cpu_mem_4_1 (.in_1(in_1), .in_2(in_2), .out_3(cpu_mem_4_1_out_3));
  CPU_ENABLE_4 cpu_enable_4_1 (.in_1(cpu_mem_4_1_out_3), .in_2(in_3), .out_3(out_4));
endmodule

module CPU_ENABLE_4 (
  input  [3:0] in_1,
  input  in_2,
  output [3:0] out_3
);

  and and_1 (out_3[0], in_1[0], in_2);
  and and_2 (out_3[1], in_1[1], in_2);
  and and_3 (out_3[2], in_1[2], in_2);
  and and_4 (out_3[3], in_1[3], in_2);
endmodule

module HalfAdder (
  input  in_1,
  input  in_2,
  output out_3,
  output out_4
);

  xor xor_1 (out_3, in_1, in_2);
  and and_1 (out_4, in_2, in_1);
endmodule

module FullAdder (
  input  in_1,
  input  in_2,
  input  in_3,
  output out_4,
  output out_5
);

  wire halfadder_1_out_3, halfadder_1_out_4, halfadder_2_out_4;

  HalfAdder halfadder_1 (.in_1(in_1), .in_2(in_2), .out_3(halfadder_1_out_3), .out_4(halfadder_1_out_4));
  HalfAdder halfadder_2 (.in_1(in_3), .in_2(halfadder_1_out_3), .out_3(out_4), .out_4(halfadder_2_out_4));
  or or_1 (out_5, halfadder_2_out_4, halfadder_1_out_4);
endmodule

module Adder4b (
  input  [3:0] in_1,
  input  in_2,
  input  [3:0] in_3,
  output out_4,
  output [3:0] out_5
);

  wire fulladder_2_out_5, fulladder_3_out_5, fulladder_4_out_5;

  FullAdder fulladder_1 (.in_1(in_1[3]), .in_2(in_3[3]), .in_3(fulladder_2_out_5), .out_5(out_4), .out_4(out_5[3]));
  FullAdder fulladder_2 (
    .in_1(in_1[2]), .in_2(in_3[2]), .in_3(fulladder_3_out_5), .out_5(fulladder_2_out_5), .out_4(out_5[2]));
  FullAdder fulladder_3 (
    .in_1(in_1[1]), .in_2(in_3[1]), .in_3(fulladder_4_out_5), .out_5(fulladder_3_out_5), .out_4(out_5[1]));
  FullAdder fulladder_4 (.in_1(in_1[0]), .in_2(in_3[0]), .in_3(in_2), .out_5(fulladder_4_out_5), .out_4(out_5[0]));
endmodule

module Decoder4x16 (
  input  a,
  input  b,
  input  c,
  input  d,
  output o1,
  output o2,
  output o3,
  output o4,
  output o5,
  output o6,
  output o7,
  output o8,
  output o9,
  output o10,
  output o11,
  output o12,
  output o13,
  output o14,
  output o15,
  output o16
);

  wire not_1_out, not_2_out, not_3_out, not_4_out;

  not not_1 (not_1_out, a);
  not not_2 (not_2_out, b);
  not not_3 (not_3_out, c);
  not not_4 (not_4_out, d);
  and and_1 (o1, a, b, c, d);
  and and_2 (o2, a, b, c, not_4_out);
  and and_3 (o3, a, b, not_3_out, d);
  and and_4 (o4, a, b, not_3_out, not_4_out);
  and and_5 (o5, a, not_2_out, c, d);
  and and_6 (o6, a, not_2_out, c, not_4_out);
  and and_7 (o7, a, not_2_out, not_3_out, d);
  and and_8 (o8, a, not_2_out, not_3_out, not_4_out);
  and and_9 (o9, not_1_out, b, c, d);
  and and_10 (o10, not_1_out, b, c, not_4_out);
  and and_11 (o11, not_1_out, b, not_3_out, d);
  and and_12 (o12, not_1_out, b, not_3_out, not_4_out);
  and and_13 (o13, not_1_out, not_2_out, c, d);
  and and_14 (o14, not_1_out, not_2_out, c, not_4_out);
  and and_15 (o15, not_1_out, not_2_out, not_3_out, d);
  and and_16 (o16, not_1_out, not_2_out, not_3_out, not_4_out);
endmodule

module SHR4bit (
  input  [3:0] in_1,
  input  in_2,
  input  in_3,
  input  in_4,
  input  in_5,
  input  in_6,
  output out_7,
  output [3:0] out_8
);

  wire [3:1] cpu_reg_4_1_out_4;

  CPU_REG_4 cpu_reg_4_1 (.in_1(in_1), .in_2(in_2), .in_3(in_4), .out_4({cpu_reg_4_1_out_4, out_7}));
  CPU_REG_4 cpu_reg_4_2 (.in_1({in_6, cpu_reg_4_1_out_4}), .in_2(in_3), .in_3(in_5), .out_4(out_8));
endmodule

module SHL4bit (
  input  [3:0] in_1,
  input  in_2,
  input  in_3,
  input  in_4,
  input  in_5,
  input  in_6,
  output out_7,
  output [3:0] out_8
);

  wire [2:0] cpu_reg_4_1_out_4;

  CPU_REG_4 cpu_reg_4_1 (.in_1(in_1), .in_2(in_2), .in_3(in_4), .out_4({out_7, cpu_reg_4_1_out_4}));
  CPU_REG_4 cpu_reg_4_2 (.in_1({cpu_reg_4_1_out_4, in_6}), .in_2(in_3), .in_3(in_5), .out_4(out_8));
endmodule

module Not4bit (
  input  [3:0] in_1,
  output [3:0] out_2
);

  not not_1 (out_2[3], in_1[3]);
  not not_2 (out_2[2], in_1[2]);
  not not_3 (out_2[1], in_1[1]);
  not not_4 (out_2[0], in_1[0]);
endmodule

module And4bit (
  input  [3:0] in_1,
  input  [3:0] in_2,
  output [3:0] out_3
);

  and and_1 (out_3[3], in_1[3], in_2[3]);
  and and_2 (out_3[2], in_1[2], in_2[2]);
  and and_3 (out_3[1], in_1[1], in_2[1]);
  and and_4 (out_3[0], in_1[0], in_2[0]);
endmodule

module Or4bit (
  input  [3:0] in_1,
  input  [3:0] in_2,
  output [3:0] out_3
);

  or or_1 (out_3[3], in_1[3], in_2[3]);
  or or_2 (out_3[2], in_1[2], in_2[2]);
  or or_3 (out_3[1], in_1[1], in_2[1]);
  or or_4 (out_3[0], in_1[0], in_2[0]);
endmodule

module XorLE1bit (
  input  a,
  input  b,
  input  a_larger,
  input  ab_eq,
  output out_5,
  output a_larger_2,
  output equal
);

  wire and_2_out, not_1_out;

  xor xor_1 (out_5, a, b);
  not not_1 (not_1_out, out_5);
  and and_1 (equal, ab_eq, not_1_out);
  and and_2 (and_2_out, ab_eq, a, out_5);
  or or_1 (a_larger_2, and_2_out, a_larger);
endmodule

module Zero4bit (
  input  [3:0] in_1,
  output out_2
);

  wire or_1_out;

  or or_1 (or_1_out, in_1[3], in_1[2], in_1[1], in_1[0]);
  not not_1 (out_2, or_1_out);
endmodule

module Xor4bit (
  input  [3:0] in_1,
  input  [3:0] in_2,
  output [3:0] out_3,
  output larger,
  output equal
);

  wire xorle1bit_1_a_larger_2, xorle1bit_1_equal, xorle1bit_2_a_larger_2, xorle1bit_2_equal,
       xorle1bit_3_a_larger_2, xorle1bit_3_equal;

  XorLE1bit xorle1bit_1 (
    .a(in_1[0]), .b(in_2[0]), .ab_eq(1'b1), .a_larger(1'b0), .out_5(out_3[0]), .equal(xorle1bit_1_equal),
    .a_larger_2(xorle1bit_1_a_larger_2));
  XorLE1bit xorle1bit_2 (
    .a(in_1[1]), .b(in_2[1]), .ab_eq(xorle1bit_1_equal), .a_larger(xorle1bit_1_a_larger_2), .out_5(out_3[1]),
    .equal(xorle1bit_2_equal), .a_larger_2(xorle1bit_2_a_larger_2));
  XorLE1bit xorle1bit_3 (
    .a(in_1[2]), .b(in_2[2]), .ab_eq(xorle1bit_2_equal), .a_larger(xorle1bit_2_a_larger_2), .out_5(out_3[2]),
    .equal(xorle1bit_3_equal), .a_larger_2(xorle1bit_3_a_larger_2));
  XorLE1bit xorle1bit_4 (
    .a(in_1[3]), .b(in_2[3]), .ab_eq(xorle1bit_3_equal), .a_larger(xorle1bit_3_a_larger_2), .out_5(out_3[3]),
    .equal(equal), .a_larger_2(larger));
endmodule
